# Fritzing sketch PCB (saved by Fritzing 0.9.3b)
circuit board: 5cm x 2.5cm

parts:
  part = Resistor [tolerance=±5% resistance=47 package=THT]
  S1 = Toggle Switch [package=THT]
  J4 = Power Jack [package=power_jack_pth_lock]
  Part2 = Adafruit Motor/Stepper/Servo Shield [part_number="Adafruit #1438"]
  LASER = LED - 5mm [color="Red (633nm)" package="5 mm [THT]"]
  MOTOR1 = Adafruit Gear-Reduced Stepper Motor (small)
  MOTOR2 = Adafruit Gear-Reduced Stepper Motor (small)
  part_2 = Resistor [tolerance=±5% resistance=10k package=THT]
  C1 = Electrolytic Capacitor [capacitance=1µF package="100 mil [THT, electrolytic]"]
  part_3 = Voltage Regulator [package=to220-igo]
  J7 = female pin header, 1 pin [form="♀ (female)"]
  J8 = female pin header, 2 pins [form="♀ (female)"]
  IRFZ44N = Basic FET N-Channel [package="TO220 [THT]"]
  J5 = Screw terminal - 2 pins [package=THT]

nets:
  N1: part.Pin_0, J7.pin1
  N2: part.Pin_1, part_2.Pin_0, IRFZ44N.gate
  N3: S1.L1, LASER.cathode, IRFZ44N.drain
  N4: S1.COM, J4.PWR, part_2.Pin_1, C1.-, part_3.GND, J8.pin1, IRFZ44N.source, J5.pin1
  N5: J4.GND, C1.+, part_3.IN, J5.pin2
  N6: Part2.M2A, MOTOR2.RED
  N7: Part2.M2B, MOTOR2.ORANGE
  N8: Part2.GND, MOTOR1.YELLOW, MOTOR2.YELLOW
  N9: Part2.M1B, MOTOR2.PINK
  N10: Part2.M1A, MOTOR2.BLUE
  N11: Part2.M3A, MOTOR1.BLUE
  N12: Part2.M3B, MOTOR1.PINK
  N13: Part2.M4B, MOTOR1.ORANGE
  N14: Part2.M4A, MOTOR1.RED
  N15: LASER.anode, part_3.OUT, J8.pin2

custom parts:
  Adafruit Motor/Stepper/Servo Shield: The original Adafruit Motorshield kit is one of our most beloved kits, which is why we decided to make something even better. We have upgraded the shield kit to make the bestest, easiest way to drive DC and Stepper motors. This shield will make quick work of your next robotics project! We kept the ability to drive up to 4 DC motors or 2 stepper motors, but added many improvements: Instead of a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
  Adafruit Gear-Reduced Stepper Motor (small): Adafruit gear-reduction stepper motor (small)
